// Logisim project 1to2demux.circ as structural Verilog: 1 circuit, main circuit main
module main (
  input  Input,
  input  Select,
  output _0,
  output _1
);

  wire not_1_out;

  not not_1 (not_1_out, Select);
  and and_1 (_0, Input, not_1_out);
  and and_2 (_1, Select, Input);

  // Notes on the sheet:
  //   1:2 DEMUX
endmodule
