// Logisim project 2to1mux.circ as structural Verilog: 1 circuit, main circuit main
module main (
  input  _0,
  input  _1,
  input  Select,
  output Output
);

  wire and_1_out, and_2_out, not_1_out;

  not not_1 (not_1_out, Select);
  and and_1 (and_1_out, _0, not_1_out);
  and and_2 (and_2_out, _1, Select);
  or or_1 (Output, and_1_out, and_2_out);

  // Notes on the sheet:
  //   2:1 MUX
endmodule
