// Logisim project fulladder.circ as structural Verilog: 2 circuits, main circuit main
module main (
  input  Cin,
  input  B,
  input  A,
  output Sum,
  output Carry_Out
);

  wire and_1_out, and_2_out, xor_1_out;

  xor xor_1 (xor_1_out, B, A);
  xor xor_2 (Sum, Cin, xor_1_out);
  and and_1 (and_1_out, xor_1_out, Cin);
  and and_2 (and_2_out, A, B);
  or or_1 (Carry_Out, and_1_out, and_2_out);

  // Notes on the sheet:
  //   FULL ADDER CIRCUIT
endmodule

module nbit (
  input  B3,
  input  B2,
  input  B1,
  input  B0,
  input  in_5,
  input  in_6,
  input  in_7,
  input  A3,
  input  A2,
  input  A1,
  input  A0,
  input  Initial_Carry_In,
  output COUT,
  output S3,
  output S2,
  output S1,
  output S0
);

  wire main_1_carry_out, main_2_carry_out, main_3_carry_out, main_4_carry_out, multiplexer_1_out,
       multiplexer_2_out, multiplexer_4_out, multiplexer_5_out, multiplexer_6_out, multiplexer_7_out,
       not_1_out, not_2_out, not_3_out, not_4_out, not_5_out, not_6_out, undriven;

  Multiplexer multiplexer_1 (.in0(in_5), .in1(in_6), .out(multiplexer_1_out), .sel(in_7));  // open: en
  not not_1 (not_1_out, B3);
  Multiplexer multiplexer_2 (.in0(B3), .in1(not_1_out), .out(multiplexer_2_out), .sel(multiplexer_1_out));  // open: en
  not not_2 (not_2_out, main_1_carry_out);
  Multiplexer multiplexer_3 (.in0(main_1_carry_out), .in1(not_2_out), .out(COUT), .sel(multiplexer_1_out));  // open: en
  main main_1 (.B(A3), .A(multiplexer_2_out), .Cin(main_2_carry_out), .Sum(S3), .Carry_Out(main_1_carry_out));
  not not_3 (not_3_out, B2);
  Multiplexer multiplexer_4 (.in0(B2), .in1(not_3_out), .out(multiplexer_4_out), .sel(multiplexer_1_out));  // open: en
  main main_2 (.B(A2), .A(multiplexer_4_out), .Cin(main_3_carry_out), .Sum(S2), .Carry_Out(main_2_carry_out));
  not not_4 (not_4_out, B1);
  Multiplexer multiplexer_5 (.in0(B1), .in1(not_4_out), .out(multiplexer_5_out), .sel(multiplexer_1_out));  // open: en
  main main_3 (.B(A1), .A(multiplexer_5_out), .Cin(main_4_carry_out), .Sum(S1), .Carry_Out(main_3_carry_out));
  Multiplexer multiplexer_6 (
    .in0(B0), .in1(not_5_out), .out(multiplexer_6_out), .sel(multiplexer_1_out), .en(undriven));
  not not_5 (not_5_out, B0);
  Multiplexer multiplexer_7 (
    .in0(Initial_Carry_In), .in1(not_6_out), .out(multiplexer_7_out), .sel(multiplexer_1_out));  // open: en
  main main_4 (.B(A0), .A(multiplexer_6_out), .Cin(multiplexer_7_out), .Sum(S0), .Carry_Out(main_4_carry_out));
  not not_6 (not_6_out, Initial_Carry_In);

  // Notes on the sheet:
  //   (1 for subtractor, 0 for adder)
  //   This Mux Decides whether its an adder or subtractor
  //   4 bit adder-subtractor
endmodule
