// Logisim project main.circ as structural Verilog: 3 circuits, main circuit Full-Adder
module Full_Adder (
  input  Cin,
  input  B,
  input  A,
  output Sum,
  output Carry_Out
);

  wire and_1_out, and_2_out, xor_1_out;

  xor xor_1 (xor_1_out, B, A);
  xor xor_2 (Sum, Cin, xor_1_out);
  and and_1 (and_1_out, xor_1_out, Cin);
  and and_2 (and_2_out, A, B);
  or or_1 (Carry_Out, and_1_out, and_2_out);

  // Notes on the sheet:
  //   FULL ADDER CIRCUIT
endmodule

module nbit (
  input  in_1,
  input  Initial_Carry_In,
  input  in_3,
  input  Enable_Input,
  output COUT,
  output S3,
  output S2,
  output S1,
  output S0
);

  wire clock_1_out, d_ff_1_q, d_ff_2_q, d_ff_3_q, d_ff_4_q, full_adder_1_carry_out, full_adder_2_carry_out,
       full_adder_3_carry_out, full_adder_4_carry_out, magnitude_comparator_1_out_9, multiplexer_1_out,
       multiplexer_2_out, multiplexer_4_out, multiplexer_5_out, multiplexer_6_out, multiplexer_7_out,
       not_1_out, not_2_out, not_3_out, not_4_out, not_5_out, not_6_out, undriven;

  Multiplexer multiplexer_1 (.in0(1'b0), .in1(1'b1), .out(multiplexer_1_out), .sel(in_1));  // open: en
  not not_1 (not_1_out, 1'b0);
  Multiplexer multiplexer_2 (
    .in0(1'b0), .in1(not_1_out), .out(multiplexer_2_out), .sel(multiplexer_1_out));  // open: en
  not not_2 (not_2_out, full_adder_1_carry_out);
  Multiplexer multiplexer_3 (
    .in0(full_adder_1_carry_out), .in1(not_2_out), .out(COUT), .sel(multiplexer_1_out));  // open: en
  Full_Adder full_adder_1 (
    .B(d_ff_1_q), .A(multiplexer_2_out), .Cin(full_adder_2_carry_out), .Sum(S3),
    .Carry_Out(full_adder_1_carry_out));
  not not_3 (not_3_out, 1'b0);
  Multiplexer multiplexer_4 (
    .in0(1'b0), .in1(not_3_out), .out(multiplexer_4_out), .sel(multiplexer_1_out));  // open: en
  Full_Adder full_adder_2 (
    .B(d_ff_2_q), .A(multiplexer_4_out), .Cin(full_adder_3_carry_out), .Sum(S2),
    .Carry_Out(full_adder_2_carry_out));
  not not_4 (not_4_out, 1'b0);
  Multiplexer multiplexer_5 (
    .in0(1'b0), .in1(not_4_out), .out(multiplexer_5_out), .sel(multiplexer_1_out));  // open: en
  Full_Adder full_adder_3 (
    .B(d_ff_3_q), .A(multiplexer_5_out), .Cin(full_adder_4_carry_out), .Sum(S1),
    .Carry_Out(full_adder_3_carry_out));
  Magnitude_Comparator magnitude_comparator_1 (
    .in_1(in_3), .in_2(S0), .in_3(in_3), .in_4(S1), .in_5(in_3), .in_6(S2), .in_7(in_3), .in_8(S3),
    .out_9(magnitude_comparator_1_out_9));
  LED led_1 (.in(magnitude_comparator_1_out_9));
  Multiplexer multiplexer_6 (
    .in0(1'b1), .in1(not_5_out), .out(multiplexer_6_out), .sel(multiplexer_1_out), .en(undriven));
  not not_5 (not_5_out, 1'b1);
  Multiplexer multiplexer_7 (
    .in0(Initial_Carry_In), .in1(not_6_out), .out(multiplexer_7_out), .sel(multiplexer_1_out));  // open: en
  Full_Adder full_adder_4 (
    .B(d_ff_4_q), .A(multiplexer_6_out), .Cin(multiplexer_7_out), .Sum(S0), .Carry_Out(full_adder_4_carry_out));
  not not_6 (not_6_out, Initial_Carry_In);
  Clock clock_1 (.out(clock_1_out));
  D_Flip_Flop d_ff_1 (
    .clk(clock_1_out), .D(S3), .Q(d_ff_1_q), .en(Enable_Input), .reset(magnitude_comparator_1_out_9));  // open: Qn, preset
  D_Flip_Flop d_ff_2 (
    .clk(clock_1_out), .D(S2), .Q(d_ff_2_q), .en(Enable_Input), .reset(magnitude_comparator_1_out_9));  // open: Qn, preset
  D_Flip_Flop d_ff_3 (
    .clk(clock_1_out), .D(S1), .Q(d_ff_3_q), .en(Enable_Input), .reset(magnitude_comparator_1_out_9));  // open: Qn, preset
  D_Flip_Flop d_ff_4 (
    .clk(clock_1_out), .D(S0), .Q(d_ff_4_q), .en(Enable_Input), .reset(magnitude_comparator_1_out_9));  // open: Qn, preset

  // Notes on the sheet:
  //   (1 for subtractor, 0 for adder)
  //   This Mux Decides whether its an adder or subtractor
  //   4 bit adder-subtractor
endmodule

module Magnitude_Comparator (
  input  in_1,
  input  in_2,
  input  in_3,
  input  in_4,
  input  in_5,
  input  in_6,
  input  in_7,
  input  in_8,
  output out_9
);

  wire xnor_1_out, xnor_2_out, xnor_3_out, xnor_4_out;

  xnor xnor_1 (xnor_1_out, in_1, in_2);
  xnor xnor_2 (xnor_2_out, in_3, in_4);
  xnor xnor_3 (xnor_3_out, in_5, in_6);
  xnor xnor_4 (xnor_4_out, in_7, in_8);
  and and_1 (out_9, xnor_1_out, xnor_2_out, xnor_3_out, xnor_4_out);

  // Notes on the sheet:
  //   Replace upper inputs with three bit output from adder-subtractor
  //   Take this o/p and use to allow i/p or not.
  //   LED to indicate full capacity
endmodule
