// Logisim project Logisim-123-146.circ as structural Verilog: 11 circuits, main circuit Equality-Check
// Is full?
module Equality_Check (
  input  in_1,
  input  in_2,
  input  in_3,
  input  in_4,
  input  in_5,
  input  in_6,
  input  in_7,
  input  in_8,
  output Is_Equal
);

  wire xnor_1_out, xnor_2_out, xnor_3_out, xnor_4_out;

  xnor xnor_1 (xnor_1_out, in_1, in_2);
  xnor xnor_2 (xnor_2_out, in_3, in_4);
  xnor xnor_3 (xnor_3_out, in_5, in_6);
  xnor xnor_4 (xnor_4_out, in_7, in_8);
  and and_1 (Is_Equal, xnor_1_out, xnor_2_out, xnor_3_out, xnor_4_out);

  // Notes on the sheet:
  //   Checking equality of 2 4-bit numbers
endmodule

// Counter
module Up_Down_Counter (
  input  Up_Down_prime,
  input  Reset,
  input  EN,
  output LSB,
  output out_5,
  output out_6,
  output MSB
);

  wire and_1_out, and_2_out, and_3_out, and_4_out, and_5_out, and_6_out, CLK_out, j_k_ff_1_qn, j_k_ff_2_qn,
       j_k_ff_3_qn, not_1_out, or_1_out, or_2_out, or_3_out;

  Clock CLK (.out(CLK_out));
  not not_1 (not_1_out, Up_Down_prime);
  J_K_Flip_Flop j_k_ff_1 (
    .J(1'b1), .clk(CLK_out), .K(1'b1), .Q(LSB), .Qn(j_k_ff_1_qn), .en(EN), .reset(Reset));  // open: preset
  and and_1 (and_1_out, Up_Down_prime, LSB);
  and and_2 (and_2_out, j_k_ff_1_qn, not_1_out, not_1_out);
  or or_1 (or_1_out, and_1_out, and_2_out);
  J_K_Flip_Flop j_k_ff_2 (
    .J(or_1_out), .clk(CLK_out), .K(or_1_out), .Q(out_5), .Qn(j_k_ff_2_qn), .en(EN), .reset(Reset));  // open: preset
  and and_3 (and_3_out, and_1_out, out_5);
  and and_4 (and_4_out, j_k_ff_2_qn, and_2_out);
  or or_2 (or_2_out, and_3_out, and_4_out);
  J_K_Flip_Flop j_k_ff_3 (
    .J(or_2_out), .clk(CLK_out), .K(or_2_out), .Q(out_6), .Qn(j_k_ff_3_qn), .en(EN), .reset(Reset));  // open: preset
  and and_5 (and_5_out, and_3_out, out_6);
  and and_6 (and_6_out, j_k_ff_3_qn, and_4_out);
  or or_3 (or_3_out, and_5_out, and_6_out);
  J_K_Flip_Flop j_k_ff_4 (
    .J(or_3_out), .clk(CLK_out), .K(or_3_out), .Q(MSB), .en(EN), .reset(Reset));  // open: Qn, preset

  // Notes on the sheet:
  //   An up-down counter used to keep track of occupancy in the waiting room.
endmodule

module Main_Circuit (
  input  in_1,
  input  _0_ADMIT_1__PATIENT_TO_DOCTOR,
  input  [1:0] ENTER_ID_OF_PATIENT_ADMITTED,
  input  [1:0] ENTER_PRIORITY_OF_PATIENT_ADMITTED,
  output [3:0] out_5,
  output [1:0] ID_OF_PATIENT_SENT_FOR_TREATMENT,
  output [1:0] PRIORITY_OF_PATIENT_SENT_FOR_TREATMENT
);

  wire and_1_out, and_2_out, equality_check_1_is_equal, multiplexer_1_out, not_1_out;
  wire [1:0] demultiplexer_1_out0;

  Demultiplexer demultiplexer_1 (
    .out0(demultiplexer_1_out0[0]), .out1(demultiplexer_1_out0[1]), .in(1'b1),
    .sel(_0_ADMIT_1__PATIENT_TO_DOCTOR), .en(in_1));
  and and_1 (and_1_out, demultiplexer_1_out0[0], not_1_out);
  Multiplexer #(.select(2)) multiplexer_1 (
    .in0(1'b0), .in1(1'b1), .in2(1'b0), .in3(1'b0), .out(multiplexer_1_out), .sel(demultiplexer_1_out0));  // open: en
  not not_1 (not_1_out, equality_check_1_is_equal);
  and and_2 (and_2_out, multiplexer_1_out, not_1_out);
  LED led_1 (.in(equality_check_1_is_equal));
  Equality_Check equality_check_1 (
    .in_1(1'b1), .in_2(out_5[0]), .in_3(1'b1), .in_4(out_5[1]), .in_5(1'b1), .in_6(out_5[2]), .in_7(1'b1),
    .in_8(out_5[3]), .Is_Equal(equality_check_1_is_equal));
  Up_Down_Counter up_down_counter_1 (
    .Up_Down_prime(and_2_out), .EN(in_1), .LSB(out_5[0]), .out_5(out_5[1]), .out_6(out_5[2]), .MSB(out_5[3]));  // open: Reset
  Output_Display output_display_1 (
    .ID(ENTER_ID_OF_PATIENT_ADMITTED), .Priority(ENTER_PRIORITY_OF_PATIENT_ADMITTED), .EN(and_1_out),
    .ID_DEQUEUED(ID_OF_PATIENT_SENT_FOR_TREATMENT), .PRIORITY_DEQUEUED(PRIORITY_OF_PATIENT_SENT_FOR_TREATMENT));

  // Notes on the sheet:
  //   Main Switch
  //   Control Switch
  //   1.Press main switch to enable the circuit
  //   INPUTS 
  //   GUIDE TO USE CIRCUIT
  //   2.To admit patient, ensure control switch is set to 0.
  //   3.To send patient for treatment(dequeue),set control switch to 1.
  //   The counter value also will have changed, confirming the dequeue.
  //   Priority 2 - Patients going to the hospital for a preplanned surgery
  //   Next, assign the ID and Priority. Run the clock twice using CTRL+T.
  //   The counter output will change confirming the admission of patient.
  //   Run the clock using CTRL+T twice, After that observe the output section.
  //   Priority 3 -Patients who have been part of a life threatening accident
  //   Priority 1 - Patients suffering from food poisoning, or a fractured limb.
  //   Priority 0 - Patients going to the hospital for a routine medical check-up
  //   NOTE:- The circuit requires a clock pulse to store values. 
  //   Please follow the instructions on how to use the clock for a successful run.
  //   LED ON INDICATES ROOM IS FULL-NO MORE PATIENTS CAN BE ADMITTED
  //   AUTOMATED HOSPITAL MANAGEMENT SYSTEM-16CO123-16CO146
  //   OUTPUTS 
  //   NUMBER OF PATIENTS IN THE ROOM (BINARY)
endmodule

// Register
module Parallel_Shift_Register (
  input  LSB_C,
  input  MSB_C,
  input  MSB,
  input  LSB,
  input  _0_enq_1_deq,
  input  EN,
  input  Reset,
  output [1:0] O_P
);

  wire Clk_out, d_ff_1_q, d_ff_2_q, d_ff_3_q, d_ff_4_q, d_ff_5_q, d_ff_6_q, d_ff_7_q, d_ff_8_q,
       demultiplexer_1_out0, demultiplexer_2_out0, demultiplexer_3_out0, demultiplexer_4_out0,
       demultiplexer_5_out0, demultiplexer_6_out0, multiplexer_1_out, multiplexer_2_out, multiplexer_4_out,
       multiplexer_5_out, multiplexer_6_out, multiplexer_7_out, multiplexer_8_out, multiplexer_9_out;
  wire [1:0] demultiplexer_2_out1, demultiplexer_4_out1, demultiplexer_6_out1, demultiplexer_8_out1;

  Clock Clk (.out(Clk_out));
  Multiplexer #(.enable("false")) multiplexer_1 (
    .in0(MSB), .in1(d_ff_1_q), .out(multiplexer_1_out), .sel(_0_enq_1_deq));
  Multiplexer #(.enable("false")) multiplexer_2 (
    .in0(LSB), .in1(d_ff_2_q), .out(multiplexer_2_out), .sel(_0_enq_1_deq));
  D_Flip_Flop d_ff_1 (.clk(Clk_out), .D(multiplexer_1_out), .Q(d_ff_1_q), .en(EN), .reset(Reset));  // open: Qn, preset
  D_Flip_Flop d_ff_2 (.clk(Clk_out), .D(multiplexer_2_out), .Q(d_ff_2_q), .en(EN), .reset(Reset));  // open: Qn, preset
  Demultiplexer #(.enable("false")) demultiplexer_1 (
    .out0(demultiplexer_1_out0), .out1(demultiplexer_2_out1[1]), .in(d_ff_1_q), .sel(_0_enq_1_deq));
  Demultiplexer #(.enable("false")) demultiplexer_2 (
    .out0(demultiplexer_2_out0), .out1(demultiplexer_2_out1[0]), .in(d_ff_2_q), .sel(_0_enq_1_deq));
  Multiplexer #(.select(2), .width(2), .enable("false")) multiplexer_3 (
    .in0(demultiplexer_2_out1), .in1(demultiplexer_4_out1), .in2(demultiplexer_6_out1),
    .in3(demultiplexer_8_out1), .out(O_P), .sel({MSB_C, LSB_C}));
  Multiplexer #(.enable("false")) multiplexer_4 (
    .in0(demultiplexer_1_out0), .in1(d_ff_3_q), .out(multiplexer_4_out), .sel(_0_enq_1_deq));
  Multiplexer #(.enable("false")) multiplexer_5 (
    .in0(demultiplexer_2_out0), .in1(d_ff_4_q), .out(multiplexer_5_out), .sel(_0_enq_1_deq));
  Demultiplexer #(.enable("false")) demultiplexer_3 (
    .out0(demultiplexer_3_out0), .out1(demultiplexer_4_out1[1]), .in(d_ff_3_q), .sel(_0_enq_1_deq));
  D_Flip_Flop d_ff_3 (.clk(Clk_out), .D(multiplexer_4_out), .Q(d_ff_3_q), .en(EN), .reset(Reset));  // open: Qn, preset
  Demultiplexer #(.enable("false")) demultiplexer_4 (
    .out0(demultiplexer_4_out0), .out1(demultiplexer_4_out1[0]), .in(d_ff_4_q), .sel(_0_enq_1_deq));
  D_Flip_Flop d_ff_4 (.clk(Clk_out), .D(multiplexer_5_out), .Q(d_ff_4_q), .en(EN), .reset(Reset));  // open: Qn, preset
  Multiplexer #(.enable("false")) multiplexer_6 (
    .in0(demultiplexer_3_out0), .in1(d_ff_5_q), .out(multiplexer_6_out), .sel(_0_enq_1_deq));
  Multiplexer #(.enable("false")) multiplexer_7 (
    .in0(demultiplexer_4_out0), .in1(d_ff_6_q), .out(multiplexer_7_out), .sel(_0_enq_1_deq));
  Demultiplexer #(.enable("false")) demultiplexer_5 (
    .out0(demultiplexer_5_out0), .out1(demultiplexer_6_out1[1]), .in(d_ff_5_q), .sel(_0_enq_1_deq));
  D_Flip_Flop d_ff_5 (.clk(Clk_out), .D(multiplexer_6_out), .Q(d_ff_5_q), .en(EN), .reset(Reset));  // open: Qn, preset
  Demultiplexer #(.enable("false")) demultiplexer_6 (
    .out0(demultiplexer_6_out0), .out1(demultiplexer_6_out1[0]), .in(d_ff_6_q), .sel(_0_enq_1_deq));
  D_Flip_Flop d_ff_6 (.clk(Clk_out), .D(multiplexer_7_out), .Q(d_ff_6_q), .en(EN), .reset(Reset));  // open: Qn, preset
  Multiplexer #(.enable("false")) multiplexer_8 (
    .in0(demultiplexer_5_out0), .in1(d_ff_7_q), .out(multiplexer_8_out), .sel(_0_enq_1_deq));
  Multiplexer #(.enable("false")) multiplexer_9 (
    .in0(demultiplexer_6_out0), .in1(d_ff_8_q), .out(multiplexer_9_out), .sel(_0_enq_1_deq));
  D_Flip_Flop d_ff_7 (.clk(Clk_out), .D(multiplexer_8_out), .Q(d_ff_7_q), .en(EN), .reset(Reset));  // open: Qn, preset
  D_Flip_Flop d_ff_8 (.clk(Clk_out), .D(multiplexer_9_out), .Q(d_ff_8_q), .en(EN), .reset(Reset));  // open: Qn, preset
  Demultiplexer #(.enable("false")) demultiplexer_7 (
    .out1(demultiplexer_8_out1[1]), .in(d_ff_7_q), .sel(_0_enq_1_deq));  // open: out0
  Demultiplexer #(.enable("false")) demultiplexer_8 (
    .out1(demultiplexer_8_out1[0]), .in(d_ff_8_q), .sel(_0_enq_1_deq));  // open: out0

  // Notes on the sheet:
  //   Counter in
  //   When the signal is given for dequeue,
  //   00
  //   01
  //   Every other element other than the one leaving the queue must remain in its respective flip-flop.
  //   Hence, we we have introduced feedback to each D flip flop that does not participate in dequeue operation
  //   10
  //   11
endmodule

// QUEUE
module Queue_Storage_Retrieval (
  input  [1:0] _2b_ID,
  input  [1:0] _2b_Priority,
  input  _1_En_0_De,
  output [1:0] O_P_00,
  output [1:0] O_P_01,
  output [1:0] O_P_10,
  output [1:0] O_P_11,
  output s0,
  output s1,
  output s2,
  output s3
);

  wire and_1_out, and_2_out, and_3_out, and_4_out, demultiplexer_1_out0, demultiplexer_1_out1,
       demultiplexer_1_out2, demultiplexer_1_out3, demultiplexer_2_out0, demultiplexer_2_out1,
       demultiplexer_2_out2, demultiplexer_2_out3, not_1_out, not_2_out,
       register_has_something_1_has_something, register_has_something_1_lsb, register_has_something_1_msb,
       register_has_something_2_has_something, register_has_something_2_lsb, register_has_something_2_msb,
       register_has_something_3_has_something, register_has_something_3_lsb, register_has_something_3_msb,
       register_has_something_4_has_something, register_has_something_4_lsb, register_has_something_4_msb;
  wire [1:0] Priority_Select_s0;

  not not_1 (not_1_out, _1_En_0_De);
  Register_Has_Something register_has_something_1 (
    .Has_something(register_has_something_1_has_something), .EN(s0), ._1_Up_0_Down(_1_En_0_De),
    .MSB(register_has_something_1_msb), .LSB(register_has_something_1_lsb));
  Parallel_Shift_Register parallel_shift_register_1 (
    .LSB_C(register_has_something_1_lsb), .MSB_C(register_has_something_1_msb), .MSB(_2b_ID[1]),
    .LSB(_2b_ID[0]), .EN(s0), .O_P(O_P_00), ._0_enq_1_deq(not_1_out));  // open: Reset
  or or_1 (s0, demultiplexer_1_out0, and_1_out);
  Register_Has_Something register_has_something_2 (
    .Has_something(register_has_something_2_has_something), .EN(s1), ._1_Up_0_Down(_1_En_0_De),
    .MSB(register_has_something_2_msb), .LSB(register_has_something_2_lsb));
  Demultiplexer #(.select(2), .enable("false")) demultiplexer_1 (
    .out0(demultiplexer_1_out0), .out1(demultiplexer_1_out1), .out2(demultiplexer_1_out2),
    .out3(demultiplexer_1_out3), .in(_1_En_0_De), .sel(_2b_Priority));
  not not_2 (not_2_out, _1_En_0_De);
  Dequeue_Priority_Select Priority_Select (
    .A3(register_has_something_4_has_something), .A2(register_has_something_3_has_something),
    .A1(register_has_something_2_has_something), .Least(register_has_something_1_has_something),
    .S1(Priority_Select_s0[1]), .S0(Priority_Select_s0[0]));
  Parallel_Shift_Register parallel_shift_register_2 (
    .LSB_C(register_has_something_2_lsb), .MSB_C(register_has_something_2_msb), .MSB(_2b_ID[1]),
    .LSB(_2b_ID[0]), .EN(s1), .O_P(O_P_01), ._0_enq_1_deq(not_1_out));  // open: Reset
  or or_2 (s1, demultiplexer_1_out1, demultiplexer_1_out1, and_2_out);
  and and_1 (and_1_out, not_2_out, demultiplexer_2_out0);
  Demultiplexer #(.select(2), .enable("false")) demultiplexer_2 (
    .out0(demultiplexer_2_out0), .out1(demultiplexer_2_out1), .out2(demultiplexer_2_out2),
    .out3(demultiplexer_2_out3), .in(1'b1), .sel(Priority_Select_s0));
  Register_Has_Something register_has_something_3 (
    .Has_something(register_has_something_3_has_something), .EN(s2), ._1_Up_0_Down(_1_En_0_De),
    .MSB(register_has_something_3_msb), .LSB(register_has_something_3_lsb));
  and and_2 (and_2_out, not_2_out, demultiplexer_2_out1);
  Parallel_Shift_Register parallel_shift_register_3 (
    .LSB_C(register_has_something_3_lsb), .MSB_C(register_has_something_3_msb), .MSB(_2b_ID[1]),
    .LSB(_2b_ID[0]), .EN(s2), .O_P(O_P_10), ._0_enq_1_deq(not_1_out));  // open: Reset
  and and_3 (and_3_out, not_2_out, demultiplexer_2_out2);
  or or_3 (s2, demultiplexer_1_out2, and_3_out);
  Register_Has_Something register_has_something_4 (
    .Has_something(register_has_something_4_has_something), .EN(s3), ._1_Up_0_Down(_1_En_0_De),
    .MSB(register_has_something_4_msb), .LSB(register_has_something_4_lsb));
  and and_4 (and_4_out, not_2_out, demultiplexer_2_out3);
  Parallel_Shift_Register parallel_shift_register_4 (
    .LSB_C(register_has_something_4_lsb), .MSB_C(register_has_something_4_msb), .MSB(_2b_ID[1]),
    .LSB(_2b_ID[0]), .EN(s3), .O_P(O_P_11), ._0_enq_1_deq(not_1_out));  // open: Reset
  or or_4 (s3, demultiplexer_1_out3, and_4_out);

  // Notes on the sheet:
  //   We have aimed to demonstrate a waiting room  with 16 patients
  //   DMX-1 determines which individual queue the patient should enter. 
  //   DMX-1
  //   Our waiting room is divided into 4 separate queues, one for each priority of patients
endmodule

module Register_Has_Something (
  input  _1_Up_0_Down,
  input  EN,
  output Has_something,
  output LSB,
  output MSB
);

  wire and_1_out, and_2_out, and_3_out, and_4_out, and_5_out, CLK_out, j_k_ff_1_qn, not_1_out, not_2_out,
       not_3_out, not_5_out, or_1_out;

  not not_1 (not_1_out, and_2_out);
  and and_1 (and_1_out, not_1_out, _1_Up_0_Down);
  Clock CLK (.out(CLK_out));
  and and_2 (and_2_out, MSB, LSB);
  not not_2 (not_2_out, and_1_out);
  not not_3 (not_3_out, LSB);
  J_K_Flip_Flop j_k_ff_1 (
    .J(1'b1), .clk(CLK_out), .K(1'b1), .Q(LSB), .Qn(j_k_ff_1_qn), .en(EN));  // open: preset, reset
  not not_4 (Has_something, and_5_out);
  and and_3 (and_3_out, and_1_out, LSB);
  and and_4 (and_4_out, j_k_ff_1_qn, not_2_out, not_2_out);
  and and_5 (and_5_out, not_3_out, not_5_out);
  or or_1 (or_1_out, and_3_out, and_4_out);
  not not_5 (not_5_out, MSB);
  J_K_Flip_Flop j_k_ff_2 (.J(or_1_out), .clk(CLK_out), .K(or_1_out), .Q(MSB), .en(EN));  // open: Qn, preset, reset

  // Notes on the sheet:
  //   This circuit tells us whether a particular queue is empty or not
endmodule

module Dequeue_Priority_Select (
  input  A3,
  input  A2,
  input  A1,
  input  Least,
  output S1,
  output S0
);

  wire and_1_out, not_1_out, not_2_out;

  not not_1 (not_1_out, A3);
  not not_2 (not_2_out, A2);
  and and_1 (and_1_out, not_2_out, not_1_out, A1);
  or or_1 (S1, A3, A2);
  or or_2 (S0, A3, and_1_out);

  // Notes on the sheet:
  //   THIS CIRCUIT UTILISES A 4b PRIORITY ENCODER LOGIC.
endmodule

module Store_Priority (
  input  LSB,
  input  in_2,
  input  in_3,
  input  in_4,
  output [3:0] out_5
);

  wire clock_1_out;

  Clock clock_1 (.out(clock_1_out));
  D_Flip_Flop d_ff_1 (.clk(clock_1_out), .D(LSB), .Q(out_5[0]));  // open: Qn, preset, en, reset
  D_Flip_Flop d_ff_2 (.clk(clock_1_out), .D(in_2), .Q(out_5[1]));  // open: Qn, preset, en, reset
  D_Flip_Flop d_ff_3 (.clk(clock_1_out), .D(in_3), .Q(out_5[2]));  // open: Qn, preset, en, reset
  D_Flip_Flop d_ff_4 (.clk(clock_1_out), .D(in_4), .Q(out_5[3]));  // open: Qn, preset, en, reset

  // Notes on the sheet:
  //   When a patient exits the hospital, the parallel shift register circuit removes the patient's information without a clock pulse.
  //   Hence, to introduce the delay required, this circuit is needed
endmodule

// Priority-Queue
module Output_Display (
  input  [1:0] ID,
  input  [1:0] Priority,
  input  EN,
  output [1:0] ID_DEQUEUED,
  output [1:0] PRIORITY_DEQUEUED
);

  wire not_1_out, queue_storage_retrieval_1_s0, queue_storage_retrieval_1_s1, queue_storage_retrieval_1_s2,
       queue_storage_retrieval_1_s3;
  wire [1:0] queue_storage_retrieval_1_o_p_00, queue_storage_retrieval_1_o_p_01,
       queue_storage_retrieval_1_o_p_10, queue_storage_retrieval_1_o_p_11;
  wire [3:0] store_priority_1_out_5;

  Queue_Storage_Retrieval queue_storage_retrieval_1 (
    ._2b_ID(ID), ._2b_Priority(Priority), .O_P_00(queue_storage_retrieval_1_o_p_00),
    .O_P_01(queue_storage_retrieval_1_o_p_01), .O_P_10(queue_storage_retrieval_1_o_p_10),
    .O_P_11(queue_storage_retrieval_1_o_p_11), ._1_En_0_De(EN), .s0(queue_storage_retrieval_1_s0),
    .s1(queue_storage_retrieval_1_s1), .s2(queue_storage_retrieval_1_s2), .s3(queue_storage_retrieval_1_s3));
  not not_1 (not_1_out, EN);
  Store_Priority store_priority_1 (
    .LSB(queue_storage_retrieval_1_s0), .in_2(queue_storage_retrieval_1_s1),
    .in_3(queue_storage_retrieval_1_s2), .in_4(queue_storage_retrieval_1_s3), .out_5(store_priority_1_out_5));
  Multiplexer #(.select(4), .width(2)) multiplexer_1 (
    .in1(2'b00), .in2(2'b01), .in4(2'b10), .in8(2'b11), .out(PRIORITY_DEQUEUED),
    .sel(store_priority_1_out_5), .en(not_1_out));  // open: in0, in3, in5, in6, in7, in9, in10, in11, in12, in13, in14, in15
  Multiplexer #(.select(2), .width(2)) multiplexer_2 (
    .in0(queue_storage_retrieval_1_o_p_00), .in1(queue_storage_retrieval_1_o_p_01),
    .in2(queue_storage_retrieval_1_o_p_10), .in3(queue_storage_retrieval_1_o_p_11), .out(ID_DEQUEUED),
    .sel(PRIORITY_DEQUEUED), .en(not_1_out));
endmodule

module _2to1mux (
  input  _0,
  input  _1,
  input  Select,
  output Output
);

  wire and_1_out, and_2_out, not_1_out;

  not not_1 (not_1_out, Select);
  and and_1 (and_1_out, _0, not_1_out);
  and and_2 (and_2_out, _1, Select);
  or or_1 (Output, and_1_out, and_2_out);

  // Notes on the sheet:
  //   2:1 MUX
endmodule

module _1to2demux (
  input  Input,
  input  Select,
  output _0,
  output _1
);

  wire not_1_out;

  not not_1 (not_1_out, Select);
  and and_1 (_0, Input, not_1_out);
  and and_2 (_1, Select, Input);

  // Notes on the sheet:
  //   1:2 DEMUX
endmodule
