// Logisim project main.circ as structural Verilog: 10 circuits, main circuit Magnitude-Comparator
// Is full?
module Magnitude_Comparator (
  input  in_1,
  input  in_2,
  input  in_3,
  input  in_4,
  input  in_5,
  input  in_6,
  input  in_7,
  input  in_8,
  output out_9
);

  wire xnor_1_out, xnor_2_out, xnor_3_out, xnor_4_out;

  xnor xnor_1 (xnor_1_out, in_1, in_2);
  xnor xnor_2 (xnor_2_out, in_3, in_4);
  xnor xnor_3 (xnor_3_out, in_5, in_6);
  xnor xnor_4 (xnor_4_out, in_7, in_8);
  and and_1 (out_9, xnor_1_out, xnor_2_out, xnor_3_out, xnor_4_out);
endmodule

// Counter
module Up_Down_Counter (
  input  Up_Down_prime,
  input  Reset,
  input  EN,
  output LSB,
  output out_5,
  output out_6,
  output MSB
);

  wire and_1_out, and_2_out, and_3_out, and_4_out, and_5_out, and_6_out, CLK_out, j_k_ff_1_qn, j_k_ff_2_qn,
       j_k_ff_3_qn, not_1_out, or_1_out, or_2_out, or_3_out;

  Clock CLK (.out(CLK_out));
  not not_1 (not_1_out, Up_Down_prime);
  J_K_Flip_Flop j_k_ff_1 (
    .J(1'b1), .clk(CLK_out), .K(1'b1), .Q(LSB), .Qn(j_k_ff_1_qn), .en(EN), .reset(Reset));  // open: preset
  and and_1 (and_1_out, Up_Down_prime, LSB);
  and and_2 (and_2_out, j_k_ff_1_qn, not_1_out, not_1_out);
  or or_1 (or_1_out, and_1_out, and_2_out);
  J_K_Flip_Flop j_k_ff_2 (
    .J(or_1_out), .clk(CLK_out), .K(or_1_out), .Q(out_5), .Qn(j_k_ff_2_qn), .en(EN), .reset(Reset));  // open: preset
  and and_3 (and_3_out, and_1_out, out_5);
  and and_4 (and_4_out, j_k_ff_2_qn, and_2_out);
  or or_2 (or_2_out, and_3_out, and_4_out);
  J_K_Flip_Flop j_k_ff_3 (
    .J(or_2_out), .clk(CLK_out), .K(or_2_out), .Q(out_6), .Qn(j_k_ff_3_qn), .en(EN), .reset(Reset));  // open: preset
  and and_5 (and_5_out, and_3_out, out_6);
  and and_6 (and_6_out, j_k_ff_3_qn, and_4_out);
  or or_3 (or_3_out, and_5_out, and_6_out);
  J_K_Flip_Flop j_k_ff_4 (
    .J(or_3_out), .clk(CLK_out), .K(or_3_out), .Q(MSB), .en(EN), .reset(Reset));  // open: Qn, preset
endmodule

module Main_Area (
  input  Main_Switch,
  input  _0_Enq_1_Deq,
  input  [1:0] ID,
  input  [1:0] Priority,
  output MSB,
  output out_6,
  output out_7,
  output LSB
);

  wire and_1_out, magnitude_comparator_1_out_9, multiplexer_1_out, not_1_out;
  wire [1:0] demultiplexer_1_out0;

  Demultiplexer demultiplexer_1 (
    .out0(demultiplexer_1_out0[0]), .out1(demultiplexer_1_out0[1]), .in(1'b1), .sel(_0_Enq_1_Deq),
    .en(Main_Switch));
  Multiplexer #(.select(2)) multiplexer_1 (
    .in0(1'b0), .in1(1'b1), .in2(1'b0), .in3(1'b0), .out(multiplexer_1_out), .sel(demultiplexer_1_out0));  // open: en
  not not_1 (not_1_out, magnitude_comparator_1_out_9);
  and and_1 (and_1_out, multiplexer_1_out, not_1_out);
  queue queue_1 (
    ._2b_ID(ID), ._2b_Priority(Priority), ._1_En_0_De(demultiplexer_1_out0[0]));  // open: out_8, out_4, out_9, out_5, out_10, out_6, out_11, out_7
  LED led_1 (.in(magnitude_comparator_1_out_9));
  Magnitude_Comparator magnitude_comparator_1 (
    .in_1(1'b1), .in_2(LSB), .in_3(1'b1), .in_4(out_7), .in_5(1'b1), .in_6(out_6), .in_7(1'b1), .in_8(MSB),
    .out_9(magnitude_comparator_1_out_9));
  Up_Down_Counter up_down_counter_1 (
    .Up_Down_prime(and_1_out), .EN(Main_Switch), .LSB(LSB), .out_5(out_7), .out_6(out_6), .MSB(MSB));  // open: Reset

  // Notes on the sheet:
  //   Use CTRL+T to run a clock pulse 
  //   NUMBER OF PATIENTS IN ROOM-BINARY OUTPUT
endmodule

// Register
module Shift_Register (
  input  MSB,
  input  in_2,
  input  in_3,
  input  LSB,
  input  EN,
  input  Reset,
  output MSB_2,
  output out_8,
  output out_9,
  output LSB_2
);

  wire CLK_out, d_ff_1_q, d_ff_2_q, d_ff_3_q, d_ff_4_q, d_ff_5_q, d_ff_6_q, d_ff_7_q, d_ff_8_q, d_ff_9_q,
       d_ff_10_q, d_ff_11_q, d_ff_12_q;

  Clock CLK (.out(CLK_out));
  D_Flip_Flop d_ff_1 (.clk(CLK_out), .D(MSB), .Q(d_ff_1_q), .en(EN), .reset(Reset));  // open: Qn, preset
  D_Flip_Flop d_ff_2 (.clk(CLK_out), .D(in_2), .Q(d_ff_2_q), .en(EN), .reset(Reset));  // open: Qn, preset
  D_Flip_Flop d_ff_3 (.clk(CLK_out), .D(in_3), .Q(d_ff_3_q), .en(EN), .reset(Reset));  // open: Qn, preset
  D_Flip_Flop d_ff_4 (.clk(CLK_out), .D(LSB), .Q(d_ff_4_q), .en(EN), .reset(Reset));  // open: Qn, preset
  D_Flip_Flop d_ff_5 (.clk(CLK_out), .D(d_ff_1_q), .Q(d_ff_5_q), .en(EN), .reset(Reset));  // open: Qn, preset
  D_Flip_Flop d_ff_6 (.clk(CLK_out), .D(d_ff_2_q), .Q(d_ff_6_q), .en(EN), .reset(Reset));  // open: Qn, preset
  D_Flip_Flop d_ff_7 (.clk(CLK_out), .D(d_ff_3_q), .Q(d_ff_7_q), .en(EN), .reset(Reset));  // open: Qn, preset
  D_Flip_Flop d_ff_8 (.clk(CLK_out), .D(d_ff_4_q), .Q(d_ff_8_q), .en(EN), .reset(Reset));  // open: Qn, preset
  D_Flip_Flop d_ff_9 (.clk(CLK_out), .D(d_ff_5_q), .Q(d_ff_9_q), .en(EN), .reset(Reset));  // open: Qn, preset
  D_Flip_Flop d_ff_10 (.clk(CLK_out), .D(d_ff_6_q), .Q(d_ff_10_q), .en(EN), .reset(Reset));  // open: Qn, preset
  D_Flip_Flop d_ff_11 (.clk(CLK_out), .D(d_ff_7_q), .Q(d_ff_11_q), .en(EN), .reset(Reset));  // open: Qn, preset
  D_Flip_Flop d_ff_12 (.clk(CLK_out), .D(d_ff_8_q), .Q(d_ff_12_q), .en(EN), .reset(Reset));  // open: Qn, preset
  D_Flip_Flop d_ff_13 (.clk(CLK_out), .D(d_ff_9_q), .Q(MSB_2), .en(EN), .reset(Reset));  // open: Qn, preset
  D_Flip_Flop d_ff_14 (.clk(CLK_out), .D(d_ff_10_q), .Q(out_8), .en(EN), .reset(Reset));  // open: Qn, preset
  D_Flip_Flop d_ff_15 (.clk(CLK_out), .D(d_ff_11_q), .Q(out_9), .en(EN), .reset(Reset));  // open: Qn, preset
  D_Flip_Flop d_ff_16 (.clk(CLK_out), .D(d_ff_12_q), .Q(LSB_2), .en(EN), .reset(Reset));  // open: Qn, preset
endmodule

module queue (
  input  [1:0] _2b_ID,
  input  [1:0] _2b_Priority,
  input  _1_En_0_De,
  output [3:0] out_4,
  output [3:0] out_5,
  output [3:0] out_6,
  output [3:0] out_7,
  output out_8,
  output out_9,
  output out_10,
  output out_11
);

  wire and_1_out, and_2_out, and_3_out, and_4_out, demultiplexer_1_out0, demultiplexer_1_out1,
       demultiplexer_1_out2, demultiplexer_1_out3, demultiplexer_2_out0, demultiplexer_2_out1,
       demultiplexer_2_out2, demultiplexer_2_out3, not_1_out, or_1_out, or_2_out, or_3_out, or_4_out;
  wire [1:0] Priority_Select_s0;

  Has_Something has_something_1 (.Has_something(out_8), .EN(or_1_out));  // open: _1_Up_0_Down
  Shift_Register shift_register_1 (
    .MSB(_2b_ID[1]), .in_2(_2b_ID[0]), .in_3(_2b_Priority[1]), .LSB(_2b_Priority[0]), .EN(or_1_out),
    .MSB_2(out_4[3]), .out_8(out_4[2]), .out_9(out_4[1]), .LSB_2(out_4[0]));  // open: Reset
  or or_1 (or_1_out, demultiplexer_1_out0, and_1_out);
  Has_Something has_something_2 (.Has_something(out_9), .EN(or_2_out));  // open: _1_Up_0_Down
  Demultiplexer #(.select(2), .enable("false")) demultiplexer_1 (
    .out0(demultiplexer_1_out0), .out1(demultiplexer_1_out1), .out2(demultiplexer_1_out2),
    .out3(demultiplexer_1_out3), .in(_1_En_0_De), .sel(_2b_Priority));
  not not_1 (not_1_out, _1_En_0_De);
  Dequeue_Priority_Select Priority_Select (
    .A3(out_11), .A2(out_10), .A1(out_9), .Least(out_8), .S1(Priority_Select_s0[1]),
    .S0(Priority_Select_s0[0]));
  Shift_Register shift_register_2 (
    .MSB(_2b_ID[1]), .in_2(_2b_ID[0]), .in_3(_2b_Priority[1]), .LSB(_2b_Priority[0]), .EN(or_2_out),
    .MSB_2(out_5[3]), .out_8(out_5[2]), .out_9(out_5[1]), .LSB_2(out_5[0]));  // open: Reset
  or or_2 (or_2_out, demultiplexer_1_out1, and_2_out);
  and and_1 (and_1_out, not_1_out, demultiplexer_2_out0);
  Demultiplexer #(.select(2), .enable("false")) demultiplexer_2 (
    .out0(demultiplexer_2_out0), .out1(demultiplexer_2_out1), .out2(demultiplexer_2_out2),
    .out3(demultiplexer_2_out3), .sel(Priority_Select_s0));  // open: in
  Has_Something has_something_3 (.Has_something(out_10), .EN(or_3_out));  // open: _1_Up_0_Down
  and and_2 (and_2_out, not_1_out, demultiplexer_2_out1);
  Shift_Register shift_register_3 (
    .MSB(_2b_ID[1]), .in_2(_2b_ID[0]), .in_3(_2b_Priority[1]), .LSB(_2b_Priority[0]), .EN(or_3_out),
    .MSB_2(out_6[3]), .out_8(out_6[2]), .out_9(out_6[1]), .LSB_2(out_6[0]));  // open: Reset
  or or_3 (or_3_out, demultiplexer_1_out2, and_3_out);
  and and_3 (and_3_out, not_1_out, demultiplexer_2_out2);
  Has_Something has_something_4 (.Has_something(out_11), .EN(or_4_out));  // open: _1_Up_0_Down
  Shift_Register shift_register_4 (
    .MSB(_2b_ID[1]), .in_2(_2b_ID[0]), .in_3(_2b_Priority[1]), .LSB(_2b_Priority[0]), .EN(or_4_out),
    .MSB_2(out_7[3]), .out_8(out_7[2]), .out_9(out_7[1]), .LSB_2(out_7[0]));  // open: Reset
  and and_4 (and_4_out, not_1_out, demultiplexer_2_out3);
  or or_4 (or_4_out, demultiplexer_1_out3, and_4_out);
endmodule

module Has_Something (
  input  _1_Up_0_Down,
  input  EN,
  output Has_something
);

  wire and_1_out, and_2_out, and_3_out, and_4_out, and_5_out, CLK_out, j_k_ff_1_q, j_k_ff_1_qn, j_k_ff_2_q,
       not_1_out, not_2_out, not_3_out, not_5_out, or_1_out;

  not not_1 (not_1_out, and_2_out);
  and and_1 (and_1_out, not_1_out, _1_Up_0_Down);
  Clock CLK (.out(CLK_out));
  and and_2 (and_2_out, j_k_ff_2_q, j_k_ff_1_q);
  not not_2 (not_2_out, and_1_out);
  not not_3 (not_3_out, j_k_ff_1_q);
  J_K_Flip_Flop j_k_ff_1 (
    .J(1'b1), .clk(CLK_out), .K(1'b1), .Q(j_k_ff_1_q), .Qn(j_k_ff_1_qn), .en(EN));  // open: preset, reset
  not not_4 (Has_something, and_5_out);
  and and_3 (and_3_out, and_1_out, j_k_ff_1_q);
  and and_4 (and_4_out, j_k_ff_1_qn, not_2_out, not_2_out);
  and and_5 (and_5_out, not_3_out, not_5_out);
  or or_1 (or_1_out, and_3_out, and_4_out);
  not not_5 (not_5_out, j_k_ff_2_q);
  J_K_Flip_Flop j_k_ff_2 (
    .J(or_1_out), .clk(CLK_out), .K(or_1_out), .Q(j_k_ff_2_q), .en(EN));  // open: Qn, preset, reset
endmodule

module Dequeue_Priority_Select (
  input  A3,
  input  A2,
  input  A1,
  input  Least,
  output S1,
  output S0
);

  wire and_1_out, not_1_out, not_2_out;

  not not_1 (not_1_out, A3);
  not not_2 (not_2_out, A2);
  and and_1 (and_1_out, not_2_out, not_1_out, A1);
  or or_1 (S1, A3, A2);
  or or_2 (S0, A3, and_1_out);
endmodule

// Register
module Backup_Register (
  input  MSB_b,
  input  in_2,
  input  in_3,
  input  LSB,
  input  EN,
  input  Reset,
  output out_7,
  output out_8,
  output out_9,
  output out_10
);

  wire CLK_out, d_ff_1_q, d_ff_2_q, d_ff_3_q, d_ff_4_q;

  Clock CLK (.out(CLK_out));
  D_Flip_Flop d_ff_1 (.clk(CLK_out), .D(MSB_b), .Q(d_ff_1_q), .en(EN), .reset(Reset));  // open: Qn, preset
  D_Flip_Flop d_ff_2 (.clk(CLK_out), .D(in_2), .Q(d_ff_2_q), .en(EN), .reset(Reset));  // open: Qn, preset
  D_Flip_Flop d_ff_3 (.clk(CLK_out), .D(in_3), .Q(d_ff_3_q), .en(EN), .reset(Reset));  // open: Qn, preset
  D_Flip_Flop d_ff_4 (.clk(CLK_out), .D(LSB), .Q(d_ff_4_q), .en(EN), .reset(Reset));  // open: Qn, preset
  D_Flip_Flop d_ff_5 (.clk(CLK_out), .D(d_ff_1_q), .Q(out_7), .en(EN), .reset(Reset));  // open: Qn, preset
  D_Flip_Flop d_ff_6 (.clk(CLK_out), .D(d_ff_2_q), .Q(out_8), .en(EN), .reset(Reset));  // open: Qn, preset
  D_Flip_Flop d_ff_7 (.clk(CLK_out), .D(d_ff_3_q), .Q(out_9), .en(EN), .reset(Reset));  // open: Qn, preset
  D_Flip_Flop d_ff_8 (.clk(CLK_out), .D(d_ff_4_q), .Q(out_10), .en(EN), .reset(Reset));  // open: Qn, preset
endmodule

module Backup_Queue (
  input  [1:0] _2b_ID,
  input  [1:0] _2b_Priority,
  input  _1_En_0_De,
  output [3:0] out_4,
  output [3:0] out_5,
  output [3:0] out_6,
  output [3:0] out_7,
  output out_8,
  output out_9,
  output out_10,
  output out_11
);

  wire and_1_out, and_2_out, and_3_out, and_4_out, demultiplexer_1_out0, demultiplexer_1_out1,
       demultiplexer_1_out2, demultiplexer_1_out3, demultiplexer_2_out0, demultiplexer_2_out1,
       demultiplexer_2_out2, demultiplexer_2_out3, not_1_out, or_1_out, or_2_out, or_3_out, or_4_out;
  wire [1:0] Priority_Select_s0;

  Has_Something has_something_1 (.Has_something(out_8), .EN(or_1_out));  // open: _1_Up_0_Down
  Backup_Register backup_register_1 (
    .MSB_b(_2b_ID[1]), .in_2(_2b_ID[0]), .in_3(_2b_Priority[1]), .LSB(_2b_Priority[0]), .EN(or_1_out),
    .out_7(out_4[3]), .out_8(out_4[2]), .out_9(out_4[1]), .out_10(out_4[0]));  // open: Reset
  or or_1 (or_1_out, demultiplexer_1_out0, and_1_out);
  Has_Something has_something_2 (.Has_something(out_9), .EN(or_2_out));  // open: _1_Up_0_Down
  Demultiplexer #(.select(2), .enable("false")) demultiplexer_1 (
    .out0(demultiplexer_1_out0), .out1(demultiplexer_1_out1), .out2(demultiplexer_1_out2),
    .out3(demultiplexer_1_out3), .in(_1_En_0_De), .sel(_2b_Priority));
  not not_1 (not_1_out, _1_En_0_De);
  Dequeue_Priority_Select Priority_Select (
    .A3(out_11), .A2(out_10), .A1(out_9), .Least(out_8), .S1(Priority_Select_s0[1]),
    .S0(Priority_Select_s0[0]));
  Backup_Register backup_register_2 (
    .MSB_b(_2b_ID[1]), .in_2(_2b_ID[0]), .in_3(_2b_Priority[1]), .LSB(_2b_Priority[0]), .EN(or_2_out),
    .out_7(out_5[3]), .out_8(out_5[2]), .out_9(out_5[1]), .out_10(out_5[0]));  // open: Reset
  or or_2 (or_2_out, demultiplexer_1_out1, and_2_out);
  and and_1 (and_1_out, not_1_out, demultiplexer_2_out0);
  Demultiplexer #(.select(2), .enable("false")) demultiplexer_2 (
    .out0(demultiplexer_2_out0), .out1(demultiplexer_2_out1), .out2(demultiplexer_2_out2),
    .out3(demultiplexer_2_out3), .sel(Priority_Select_s0));  // open: in
  Has_Something has_something_3 (.Has_something(out_10), .EN(or_3_out));  // open: _1_Up_0_Down
  and and_2 (and_2_out, not_1_out, demultiplexer_2_out1);
  Backup_Register backup_register_3 (
    .MSB_b(_2b_ID[1]), .in_2(_2b_ID[0]), .in_3(_2b_Priority[1]), .LSB(_2b_Priority[0]), .EN(or_3_out),
    .out_7(out_6[3]), .out_8(out_6[2]), .out_9(out_6[1]), .out_10(out_6[0]));  // open: Reset
  or or_3 (or_3_out, demultiplexer_1_out2, and_3_out);
  and and_3 (and_3_out, not_1_out, demultiplexer_2_out2);
  Has_Something has_something_4 (.Has_something(out_11), .EN(or_4_out));  // open: _1_Up_0_Down
  Backup_Register backup_register_4 (
    .MSB_b(_2b_ID[1]), .in_2(_2b_ID[0]), .in_3(_2b_Priority[1]), .LSB(_2b_Priority[0]), .EN(or_4_out),
    .out_7(out_7[3]), .out_8(out_7[2]), .out_9(out_7[1]), .out_10(out_7[0]));  // open: Reset
  and and_4 (and_4_out, not_1_out, demultiplexer_2_out3);
  or or_4 (or_4_out, demultiplexer_1_out3, and_4_out);
endmodule

// Dequeued element
module new_Shift_Register (
  input  in_1,
  input  in_2,
  input  MSB_b,
  input  in_4,
  input  in_5,
  input  LSB,
  input  En_0__Deq_1,
  input  EN,
  input  Reset,
  output [3:0] out_10,
  output out_11,
  output out_12,
  output out_13,
  output out_14
);

  wire CLK_out, d_ff_1_q, d_ff_3_q, d_ff_4_q, demultiplexer_1_out0, demultiplexer_2_out0,
       demultiplexer_3_out0, demultiplexer_4_out0, multiplexer_1_out, multiplexer_2_out, multiplexer_3_out,
       multiplexer_4_out;
  wire [3:0] demultiplexer_4_out1;

  Multiplexer #(.enable("false")) multiplexer_1 (
    .in0(MSB_b), .in1(d_ff_1_q), .out(multiplexer_1_out), .sel(En_0__Deq_1));
  Multiplexer #(.enable("false")) multiplexer_2 (
    .in0(in_4), .in1(En_0__Deq_1), .out(multiplexer_2_out), .sel(En_0__Deq_1));
  Multiplexer #(.enable("false")) multiplexer_3 (
    .in0(in_5), .in1(d_ff_3_q), .out(multiplexer_3_out), .sel(En_0__Deq_1));
  Multiplexer #(.enable("false")) multiplexer_4 (.in0(LSB), .in1(d_ff_4_q), .out(multiplexer_4_out), .sel(En_0__Deq_1));
  Clock CLK (.out(CLK_out));
  Demultiplexer #(.enable("false")) demultiplexer_1 (
    .out0(demultiplexer_1_out0), .out1(demultiplexer_4_out1[3]), .in(d_ff_1_q), .sel(En_0__Deq_1));
  D_Flip_Flop d_ff_1 (.clk(CLK_out), .D(multiplexer_1_out), .Q(d_ff_1_q), .en(EN), .reset(Reset));  // open: Qn, preset
  Demultiplexer #(.enable("false")) demultiplexer_2 (
    .out0(demultiplexer_2_out0), .out1(demultiplexer_4_out1[2]), .in(En_0__Deq_1), .sel(En_0__Deq_1));
  D_Flip_Flop d_ff_2 (
    .clk(CLK_out), .D(multiplexer_2_out), .Q(En_0__Deq_1), .en(EN), .reset(Reset));  // open: Qn, preset
  D_Flip_Flop d_ff_3 (.clk(CLK_out), .D(multiplexer_3_out), .Q(d_ff_3_q), .en(EN), .reset(Reset));  // open: Qn, preset
  Demultiplexer #(.enable("false")) demultiplexer_3 (
    .out0(demultiplexer_3_out0), .out1(demultiplexer_4_out1[1]), .in(d_ff_3_q), .sel(En_0__Deq_1));
  D_Flip_Flop d_ff_4 (.clk(CLK_out), .D(multiplexer_4_out), .Q(d_ff_4_q), .en(EN), .reset(Reset));  // open: Qn, preset
  Demultiplexer #(.enable("false")) demultiplexer_4 (
    .out0(demultiplexer_4_out0), .out1(demultiplexer_4_out1[0]), .in(d_ff_4_q), .sel(En_0__Deq_1));
  Multiplexer #(.select(2), .width(4), .enable("false")) multiplexer_5 (
    .in0(demultiplexer_4_out1), .out(out_10), .sel({in_2, in_1}));  // open: in1, in2, in3
  D_Flip_Flop d_ff_5 (.clk(CLK_out), .D(demultiplexer_1_out0), .Q(out_11), .en(EN), .reset(Reset));  // open: Qn, preset
  D_Flip_Flop d_ff_6 (.clk(CLK_out), .D(demultiplexer_2_out0), .Q(out_12), .en(EN), .reset(Reset));  // open: Qn, preset
  D_Flip_Flop d_ff_7 (.clk(CLK_out), .D(demultiplexer_3_out0), .Q(out_13), .en(EN), .reset(Reset));  // open: Qn, preset
  D_Flip_Flop d_ff_8 (.clk(CLK_out), .D(demultiplexer_4_out0), .Q(out_14), .en(EN), .reset(Reset));  // open: Qn, preset

  // Notes on the sheet:
  //   these are inputs from counter
  //   They'll take care of FIFO
  //   MUX1
  //   Dequeeud element
  //   I've just tried it on smaller number of elements. 
  //   In real scenario, the trigger for feedback needs to be dequeue AND NOT mux1
endmodule
