// Logisim project newshiftreg.circ as structural Verilog: 1 circuit, main circuit main
module main (
  input  LSB,
  input  MSB,
  input  MSB_2,
  input  LSB_2,
  input  Enq_0__Deq_1,
  input  EN,
  input  Reset,
  output [1:0] out_8
);

  wire Clk_out, d_ff_1_q, d_ff_2_q, d_ff_3_q, d_ff_4_q, d_ff_5_q, d_ff_6_q, d_ff_7_q, d_ff_8_q,
       demultiplexer_1_out0, demultiplexer_2_out0, demultiplexer_3_out0, demultiplexer_4_out0,
       demultiplexer_5_out0, demultiplexer_6_out0, multiplexer_1_out, multiplexer_2_out, multiplexer_4_out,
       multiplexer_5_out, multiplexer_6_out, multiplexer_7_out, multiplexer_8_out, multiplexer_9_out;
  wire [1:0] demultiplexer_2_out1, demultiplexer_4_out1, demultiplexer_6_out1, demultiplexer_8_out1;

  Clock Clk (.out(Clk_out));
  Multiplexer #(.enable("false")) multiplexer_1 (
    .in0(MSB_2), .in1(d_ff_1_q), .out(multiplexer_1_out), .sel(Enq_0__Deq_1));
  Multiplexer #(.enable("false")) multiplexer_2 (
    .in0(LSB_2), .in1(d_ff_2_q), .out(multiplexer_2_out), .sel(Enq_0__Deq_1));
  D_Flip_Flop d_ff_1 (.clk(Clk_out), .D(multiplexer_1_out), .Q(d_ff_1_q), .en(EN), .reset(Reset));  // open: Qn, preset
  D_Flip_Flop d_ff_2 (.clk(Clk_out), .D(multiplexer_2_out), .Q(d_ff_2_q), .en(EN), .reset(Reset));  // open: Qn, preset
  Demultiplexer #(.enable("false")) demultiplexer_1 (
    .out0(demultiplexer_1_out0), .out1(demultiplexer_2_out1[1]), .in(d_ff_1_q), .sel(Enq_0__Deq_1));
  Demultiplexer #(.enable("false")) demultiplexer_2 (
    .out0(demultiplexer_2_out0), .out1(demultiplexer_2_out1[0]), .in(d_ff_2_q), .sel(Enq_0__Deq_1));
  Multiplexer #(.select(2), .width(2), .enable("false")) multiplexer_3 (
    .in0(demultiplexer_2_out1), .in1(demultiplexer_4_out1), .in2(demultiplexer_6_out1),
    .in3(demultiplexer_8_out1), .out(out_8), .sel({MSB, LSB}));
  Multiplexer #(.enable("false")) multiplexer_4 (
    .in0(demultiplexer_1_out0), .in1(d_ff_3_q), .out(multiplexer_4_out), .sel(Enq_0__Deq_1));
  Multiplexer #(.enable("false")) multiplexer_5 (
    .in0(demultiplexer_2_out0), .in1(d_ff_4_q), .out(multiplexer_5_out), .sel(Enq_0__Deq_1));
  Demultiplexer #(.enable("false")) demultiplexer_3 (
    .out0(demultiplexer_3_out0), .out1(demultiplexer_4_out1[1]), .in(d_ff_3_q), .sel(Enq_0__Deq_1));
  D_Flip_Flop d_ff_3 (.clk(Clk_out), .D(multiplexer_4_out), .Q(d_ff_3_q), .en(EN), .reset(Reset));  // open: Qn, preset
  Demultiplexer #(.enable("false")) demultiplexer_4 (
    .out0(demultiplexer_4_out0), .out1(demultiplexer_4_out1[0]), .in(d_ff_4_q), .sel(Enq_0__Deq_1));
  D_Flip_Flop d_ff_4 (.clk(Clk_out), .D(multiplexer_5_out), .Q(d_ff_4_q), .en(EN), .reset(Reset));  // open: Qn, preset
  Multiplexer #(.enable("false")) multiplexer_6 (
    .in0(demultiplexer_3_out0), .in1(d_ff_5_q), .out(multiplexer_6_out), .sel(Enq_0__Deq_1));
  Multiplexer #(.enable("false")) multiplexer_7 (
    .in0(demultiplexer_4_out0), .in1(d_ff_6_q), .out(multiplexer_7_out), .sel(Enq_0__Deq_1));
  D_Flip_Flop d_ff_5 (.clk(Clk_out), .D(multiplexer_6_out), .Q(d_ff_5_q), .en(EN), .reset(Reset));  // open: Qn, preset
  Demultiplexer #(.enable("false")) demultiplexer_5 (
    .out0(demultiplexer_5_out0), .out1(demultiplexer_6_out1[1]), .in(d_ff_5_q), .sel(Enq_0__Deq_1));
  D_Flip_Flop d_ff_6 (.clk(Clk_out), .D(multiplexer_7_out), .Q(d_ff_6_q), .en(EN), .reset(Reset));  // open: Qn, preset
  Demultiplexer #(.enable("false")) demultiplexer_6 (
    .out0(demultiplexer_6_out0), .out1(demultiplexer_6_out1[0]), .in(d_ff_6_q), .sel(Enq_0__Deq_1));
  Multiplexer #(.enable("false")) multiplexer_8 (
    .in0(demultiplexer_5_out0), .in1(d_ff_7_q), .out(multiplexer_8_out), .sel(Enq_0__Deq_1));
  Multiplexer #(.enable("false")) multiplexer_9 (
    .in0(demultiplexer_6_out0), .in1(d_ff_8_q), .out(multiplexer_9_out), .sel(Enq_0__Deq_1));
  D_Flip_Flop d_ff_7 (.clk(Clk_out), .D(multiplexer_8_out), .Q(d_ff_7_q), .en(EN), .reset(Reset));  // open: Qn, preset
  D_Flip_Flop d_ff_8 (.clk(Clk_out), .D(multiplexer_9_out), .Q(d_ff_8_q), .en(EN), .reset(Reset));  // open: Qn, preset
  Demultiplexer #(.enable("false")) demultiplexer_7 (
    .out1(demultiplexer_8_out1[1]), .in(d_ff_7_q), .sel(Enq_0__Deq_1));  // open: out0
  Demultiplexer #(.enable("false")) demultiplexer_8 (
    .out1(demultiplexer_8_out1[0]), .in(d_ff_8_q), .sel(Enq_0__Deq_1));  // open: out0

  // Notes on the sheet:
  //   Counter in
  //   00
  //   01
  //   10
  //   11
endmodule
